// Logisim project Projeto de Circuitos XOF.circ as structural Verilog: 6 circuits, main circuit main
module main (
  input  [3:0] in_1,
  input  [3:0] in_2,
  input  [3:0] in_3,
  input  [3:0] in_4,
  input  in_5,
  input  in_6,
  input  in_7,
  input  in_8,
  input  in_9,
  input  in_10,
  input  in_11,
  input  in_12
);

  wire A_ganhou, A_jogando, A_Out, ACERTOU, and_1_out, and_4_out, and_5_out, and_6_out, and_7_out,
       and_10_out, and_11_out, and_13_out, and_14_out, and_16_out, and_17_out, and_18_out, and_21_out,
       and_22_out, and_23_out, and_27_out, and_28_out, and_29_out, and_30_out, and_31_out, and_32_out,
       and_33_out, and_35_out, and_36_out, and_37_out, and_38_out, and_39_out, and_41_out, and_42_out,
       and_43_out, and_45_out, and_46_out, B_ganhou, B_jogando, B_Out, buffer_1_out, buffer_2_out,
       buffer_3_out, buffer_4_out, buffer_5_out, buffer_6_out, buffer_7_out, buffer_8_out, buffer_9_out,
       buffer_10_out, buffer_11_out, buffer_12_out, buffer_13_out, buffer_14_out, buffer_15_out,
       buffer_16_out, buffer_17_out, buffer_18_out, buffer_19_out, buffer_20_out, buffer_21_out,
       buffer_22_out, buffer_23_out, buffer_24_out, buffer_25_out, buffer_26_out, buffer_27_out,
       buffer_28_out, buffer_29_out, buffer_30_out, buffer_31_out, buffer_32_out, buffer_33_out,
       buffer_34_out, buffer_35_out, buffer_36_out, buffer_38_out, buffer_39_out, buffer_40_out,
       buffer_41_out, buffer_42_out, buffer_43_out, buffer_44_out, buffer_45_out, buffer_46_out,
       buffer_47_out, button_8_out, Chutando_X, Chutando_Y, Chutar, Clear, CLK, clock_1_out, clr,
       comparator_1_eq, comparator_1_gt, comparator_1_lt, comparator_2_eq, comparator_2_gt, comparator_2_lt,
       comparator_3_eq, comparator_4_eq, Config, cont_0_5_2_c_out, cont_0_5_4_c_out, cont_0_9_1_c_out,
       cont_0_9_2_c_out, cont_0_9_3_c_out, cont_0_9_4_c_out, EMPATE, FIM_DE_JOGO, IGUAL, Jogador, MAIOR,
       MENOR, nand_1_out, nand_2_out, nand_3_out, nand_4_out, nand_5_out, nand_6_out, nand_7_out, nand_8_out,
       nor_1_out, nor_2_out, nor_3_out, nor_4_out, nor_5_out, nor_6_out, nor_7_out, nor_8_out, On, or_1_out,
       or_4_out, or_5_out, or_6_out, or_8_out, or_9_out, Preset, prst, \PRÓXIMO , \Próximo_t , RESET, START,
       SX, SY, toggle_2_out_3, toggle_3_out_3, tunnel;
  wire [1:0] d_ff_2_q, state;
  wire [2:0] Xr, Yr;
  wire [3:0] adder_4_out, adder_5_out, DA, DB, DMA, DMB, DSA, DSB, multiplexer_5_out, PA, PB,
       subtractor_1_out, subtractor_2_out, subtractor_3_out, subtractor_4_out, UMA, UMB, USA, USB, X, Xo, Y,
       Yo;
  wire [3:3] multiplexer_3_out, multiplexer_4_out;
  wire [4:0] adder_1_out, adder_2_out, bit_extender_1_out, bit_extender_2_out, bit_extender_3_out,
       bit_extender_4_out, bit_extender_5_out, bit_extender_6_out;

  Button button_1 (.out(Clear));
  Button button_2 (.out(Preset));
  Hex_Digit_Display hex_digit_display_1 (.value(DMA));  // open: dp
  LED led_1 (.in(in_9));
  and and_1 (and_1_out, nor_1_out, buffer_1_out);
  nor nor_1 (nor_1_out, DMA[0], DMA[1], DMA[2], DMA[3]);
  nand nand_1 (nand_1_out, DMA[0], DMA[1], DMA[2], DMA[3]);
  Clock clock_1 (.out(clock_1_out));
  assign bit_extender_1_out = {{1{1'b0}}, PA};  // Bit_Extender bit_extender_1
  assign bit_extender_2_out = {{1{1'b0}}, PB};  // Bit_Extender bit_extender_2
  Hex_Digit_Display hex_digit_display_2 (.value(PA));  // open: dp
  LED led_2 (.in(CLK));
  LED led_3 (.in(CLK));
  Hex_Digit_Display hex_digit_display_3 (.value(UMA));  // open: dp
  Hex_Digit_Display hex_digit_display_4 (.value(DA));  // open: dp
  LED led_4 (.in(A_jogando));
  Hex_Digit_Display hex_digit_display_5 (.value(Xo));  // open: dp
  buf buffer_1 (buffer_1_out, buffer_2_out);
  buf buffer_2 (buffer_2_out, buffer_3_out);
  buf buffer_3 (buffer_3_out, buffer_4_out);
  buf buffer_4 (buffer_4_out, buffer_5_out);
  buf buffer_5 (buffer_5_out, nand_1_out);
  cont_0_5 cont_0_5_1 (
    .CLK(cont_0_9_1_c_out), .Enable(A_jogando), .Clear(clr), .Preset_value(in_1), .Q(DMA), .Preset(prst));  // open: C_out
  and and_2 (CLK, ~FIM_DE_JOGO, clock_1_out);  // AND_Gate
  and and_3 (\Próximo_t , \PRÓXIMO , ~buffer_7_out);  // AND_Gate
  buf buffer_6 (buffer_6_out, \PRÓXIMO );
  buf buffer_7 (buffer_7_out, buffer_6_out);
  and and_4 (and_4_out, ~Jogador, On);  // AND_Gate
  and and_5 (and_5_out, Jogador, On);
  and and_6 (and_6_out, state[0], state[1], \Próximo_t , ACERTOU);
  Subtractor #(.width(4)) subtractor_1 (.a(4'b1000), .b({1'b0, X[2:0]}), .out(subtractor_1_out));  // open: bin, bout
  Subtractor #(.width(4)) subtractor_2 (.a(4'b1000), .b({1'b0, Y[2:0]}), .out(subtractor_2_out));  // open: bin, bout
  assign bit_extender_3_out = {{1{Xo[3]}}, Xo};  // Bit_Extender bit_extender_3
  assign bit_extender_4_out = {{1{Yo[3]}}, Yo};  // Bit_Extender bit_extender_4
  Comparator #(.width(5)) comparator_1 (
    .a(bit_extender_1_out), .b(bit_extender_2_out), .gt(comparator_1_gt), .eq(comparator_1_eq),
    .lt(comparator_1_lt));
  Hex_Digit_Display hex_digit_display_6 (.value(DSA));  // open: dp
  Hex_Digit_Display hex_digit_display_7 (.value(USA));  // open: dp
  Hex_Digit_Display hex_digit_display_8 (.value(Yo));  // open: dp
  and and_7 (and_7_out, nor_2_out, buffer_8_out);
  buf buffer_8 (buffer_8_out, buffer_9_out);
  buf buffer_9 (buffer_9_out, buffer_10_out);
  buf buffer_10 (buffer_10_out, buffer_11_out);
  nor nor_2 (nor_2_out, UMA[0], UMA[1], UMA[2], UMA[3]);
  buf buffer_11 (buffer_11_out, buffer_12_out);
  buf buffer_12 (buffer_12_out, nand_2_out);
  nand nand_2 (nand_2_out, UMA[0], UMA[1], UMA[2], UMA[3]);
  cont_0_9 cont_0_9_1 (
    .CLK(cont_0_5_2_c_out), .Enable(A_jogando), .Clear(clr), .Preset_value(in_2), .Q(UMA),
    .C_out(cont_0_9_1_c_out), .Preset(prst));
  and and_8 (A_jogando, ~A_Out, and_4_out);  // AND_Gate
  and and_9 (B_jogando, and_5_out, ~B_Out);  // AND_Gate
  Multiplexer #(.width(4), .disabled(0), .enable("false")) multiplexer_1 (
    .in0({1'b0, in_10, in_11, in_12}), .in1(subtractor_3_out), .out(DA), .sel(in_9));
  Subtractor #(.width(4)) subtractor_3 (
    .a(4'b1000), .b({1'b0, in_10, in_11, in_12}), .out(subtractor_3_out));  // open: bin, bout
  Multiplexer #(.width(4), .disabled(0), .enable("false")) multiplexer_2 (
    .in0({1'b0, in_6, in_7, in_8}), .in1(subtractor_4_out), .out(DB), .sel(in_5));
  Subtractor #(.width(4)) subtractor_4 (
    .a(4'b1000), .b({1'b0, in_6, in_7, in_8}), .out(subtractor_4_out));  // open: bin, bout
  Random #(.width(4)) random_1 (.clk(or_1_out), .out(Xo));  // open: next, clr
  or or_1 (or_1_out, and_6_out, RESET);
  Random #(.width(4), .seed(1)) random_2 (.clk(or_1_out), .out(Yo));  // open: next, clr
  Multiplexer #(.width(4), .disabled(0), .enable("false")) multiplexer_3 (
    .in0({1'b0, X[2:0]}), .in1(subtractor_1_out), .out({multiplexer_3_out[3], Xr}), .sel(SX));
  Multiplexer #(.width(4), .disabled(0), .enable("false")) multiplexer_4 (
    .in0({1'b0, Y[2:0]}), .in1(subtractor_2_out), .out({multiplexer_4_out[3], Yr}), .sel(SY));
  Adder #(.width(5)) adder_1 (.a(bit_extender_3_out), .b(bit_extender_4_out), .out(adder_1_out));  // open: cin, cout
  and and_10 (and_10_out, PA[3], PA[2], PA[1], PA[0]);
  and and_11 (and_11_out, comparator_1_gt, FIM_DE_JOGO);
  and and_12 (EMPATE, comparator_1_eq, FIM_DE_JOGO);
  and and_13 (and_13_out, comparator_1_lt, FIM_DE_JOGO);
  and and_14 (and_14_out, PB[3], PB[2], PB[1], PB[0]);
  LED led_5 (.in(A_ganhou));
  and and_15 (A_Out, and_1_out, and_7_out, and_16_out, and_17_out);
  cont_0_5 cont_0_5_2 (
    .CLK(cont_0_9_2_c_out), .Enable(A_jogando), .Clear(clr), .Preset_value(in_3), .Q(DSA),
    .C_out(cont_0_5_2_c_out), .Preset(prst));
  or or_2 (A_ganhou, and_10_out, and_11_out);
  or or_3 (B_ganhou, and_13_out, and_14_out);
  Button button_3 (.out(START));
  LED led_6 (.in(MAIOR));
  Button button_4 (.out(\PRÓXIMO ));
  LED led_7 (.in(SX));
  Hex_Digit_Display hex_digit_display_9 (.value(X));  // open: dp
  LED led_8 (.in(Chutando_X));
  and and_16 (and_16_out, nor_3_out, buffer_13_out);
  buf buffer_13 (buffer_13_out, buffer_14_out);
  buf buffer_14 (buffer_14_out, buffer_15_out);
  buf buffer_15 (buffer_15_out, buffer_16_out);
  nor nor_3 (nor_3_out, DSA[0], DSA[1], DSA[2], DSA[3]);
  buf buffer_16 (buffer_16_out, buffer_17_out);
  buf buffer_17 (buffer_17_out, nand_3_out);
  nand nand_3 (nand_3_out, DSA[0], DSA[1], DSA[2], DSA[3]);
  cont_0_9 cont_0_9_2 (
    .CLK(CLK), .Enable(A_jogando), .Clear(clr), .Preset_value(in_4), .Q(USA), .C_out(cont_0_9_2_c_out),
    .Preset(prst));
  assign bit_extender_5_out = {{1{SX}}, {SX, Xr}};  // Bit_Extender bit_extender_5
  assign bit_extender_6_out = {{1{SY}}, {SY, Yr}};  // Bit_Extender bit_extender_6
  LED led_9 (.in(EMPATE));
  LED led_10 (.in(FIM_DE_JOGO));
  LED led_11 (.in(tunnel));
  Button button_5 (.out(Config));
  Button button_6 (.out(RESET));
  LED led_12 (.in(ACERTOU));
  LED led_13 (.in(IGUAL));
  Button button_7 (.out(Chutar));
  LED led_14 (.in(SY));
  Hex_Digit_Display hex_digit_display_10 (.value(Y));  // open: dp
  LED led_15 (.in(Chutando_Y));
  and and_17 (and_17_out, nor_4_out, buffer_18_out);
  nor nor_4 (nor_4_out, USA[0], USA[1], USA[2], USA[3]);
  nand nand_4 (nand_4_out, USA[0], USA[1], USA[2], USA[3]);
  Adder #(.width(5)) adder_2 (.a(bit_extender_5_out), .b(bit_extender_6_out), .out(adder_2_out));  // open: cin, cout
  Comparator #(.width(5)) comparator_2 (
    .a(adder_2_out), .b(adder_1_out), .gt(comparator_2_gt), .eq(comparator_2_eq), .lt(comparator_2_lt));
  Comparator #(.width(4)) comparator_3 (.a({SX, Xr}), .b(Xo), .eq(comparator_3_eq));  // open: gt, lt
  Comparator #(.width(4)) comparator_4 (.a({SY, Yr}), .b(Yo), .eq(comparator_4_eq));  // open: gt, lt
  LED led_16 (.in(B_ganhou));
  LED led_17 (.in(MENOR));
  buf buffer_18 (buffer_18_out, buffer_19_out);
  buf buffer_19 (buffer_19_out, buffer_20_out);
  buf buffer_20 (buffer_20_out, buffer_21_out);
  buf buffer_21 (buffer_21_out, buffer_22_out);
  buf buffer_22 (buffer_22_out, nand_4_out);
  D_Flip_Flop d_ff_1 (.clk(and_18_out), .D(state[1]), .Q(d_ff_2_q[1]), .reset(or_4_out));  // open: Qn, preset, en
  and and_18 (and_18_out, \Próximo_t , ~FIM_DE_JOGO, On);  // AND_Gate
  or or_4 (or_4_out, RESET, and_29_out);
  and and_19 (Chutando_X, state[0], ~state[1]);  // AND_Gate
  and and_20 (Chutando_Y, ~state[0], state[1]);  // AND_Gate
  and and_21 (and_21_out, in_9, ~Jogador);  // AND_Gate
  and and_22 (and_22_out, in_5, Jogador);
  and and_23 (and_23_out, state[1], state[0]);
  and and_24 (MAIOR, and_23_out, comparator_2_gt);
  and and_25 (IGUAL, and_23_out, comparator_2_eq);
  and and_26 (MENOR, and_23_out, comparator_2_lt);
  and and_27 (and_27_out, state[1], state[0]);
  buf buffer_23 (buffer_23_out, buffer_24_out);
  buf buffer_24 (buffer_24_out, buffer_26_out);
  and and_28 (and_28_out, ~buffer_23_out, comparator_3_eq, and_27_out, comparator_4_eq);  // AND_Gate
  Hex_Digit_Display hex_digit_display_11 (.value(UMB));  // open: dp
  Hex_Digit_Display hex_digit_display_12 (.value(DMB));  // open: dp
  D_Flip_Flop d_ff_2 (.clk(and_18_out), .D(state[0]), .Q(d_ff_2_q[0]), .reset(or_4_out));  // open: Qn, preset, en
  and and_29 (and_29_out, ~state[1], ~state[0]);  // AND_Gate
  toggle toggle_1 (.in_1(START), .out_3(On), .in_2(RESET));
  toggle toggle_2 (.in_1(Config), .out_3(toggle_2_out_3), .in_2(RESET));
  and and_30 (and_30_out, Chutar, ~FIM_DE_JOGO);  // AND_Gate
  and and_31 (and_31_out, and_30_out, Chutando_X);
  and and_32 (and_32_out, Chutando_Y, and_30_out);
  or or_5 (or_5_out, and_21_out, and_22_out);
  buf buffer_25 (buffer_25_out, ACERTOU);
  buf buffer_26 (buffer_26_out, buffer_25_out);
  or or_6 (or_6_out, and_28_out, and_33_out);
  and and_33 (and_33_out, \Próximo_t , ACERTOU);
  Hex_Digit_Display hex_digit_display_13 (.value(PB));  // open: dp
  LED led_18 (.in(CLK));
  LED led_19 (.in(CLK));
  Hex_Digit_Display hex_digit_display_14 (.value(DSB));  // open: dp
  LED led_20 (.in(in_5));
  Hex_Digit_Display hex_digit_display_15 (.value(DB));  // open: dp
  nor nor_5 (nor_5_out, DMB[0], DMB[1], DMB[2], DMB[3]);
  nand nand_5 (nand_5_out, DMB[0], DMB[1], DMB[2], DMB[3]);
  Adder #(.width(2)) adder_3 (.a(d_ff_2_q), .b(2'b01), .out(state));  // open: cin, cout
  toggle toggle_3 (.in_1(and_29_out), .out_3(toggle_3_out_3), .in_2(RESET));
  and and_34 (tunnel, ~On, toggle_2_out_3);  // AND_Gate
  D_Flip_Flop d_ff_3 (.clk(and_31_out), .D(or_5_out), .Q(SX), .reset(RESET));  // open: Qn, preset, en
  D_Flip_Flop d_ff_4 (.clk(and_32_out), .D(or_5_out), .Q(SY), .reset(RESET));  // open: Qn, preset, en
  toggle toggle_4 (.in_1(or_6_out), .out_3(ACERTOU), .in_2(RESET));
  Button button_8 (.out(button_8_out));
  and and_35 (and_35_out, ACERTOU, ~Jogador);  // AND_Gate
  and and_36 (and_36_out, ACERTOU, Jogador);
  Hex_Digit_Display hex_digit_display_16 (.value(USB));  // open: dp
  LED led_21 (.in(B_jogando));
  and and_37 (and_37_out, nor_5_out, buffer_27_out);
  buf buffer_27 (buffer_27_out, buffer_28_out);
  buf buffer_28 (buffer_28_out, buffer_29_out);
  buf buffer_29 (buffer_29_out, buffer_30_out);
  buf buffer_30 (buffer_30_out, buffer_31_out);
  buf buffer_31 (buffer_31_out, nand_5_out);
  cont_0_5 cont_0_5_3 (
    .CLK(cont_0_9_3_c_out), .Enable(B_jogando), .Clear(clr), .Preset_value(in_1), .Q(DMB), .Preset(prst));  // open: C_out
  or or_7 (FIM_DE_JOGO, A_ganhou, and_38_out, B_ganhou);
  and and_38 (and_38_out, A_Out, B_Out);
  and and_39 (and_39_out, Clear, tunnel);
  and and_40 (prst, Preset, tunnel);
  _4bit_mem u_4bit_mem_1 (
    .CLK(and_31_out), .Enable(On), .Clear(RESET), .Preset(1'b0), .Q(X), .D(multiplexer_5_out));  // open: Preset_value
  _4bit_mem u_4bit_mem_2 (
    .CLK(and_32_out), .Enable(On), .Clear(RESET), .Preset(1'b0), .Q(Y), .D(multiplexer_5_out));  // open: Preset_value
  or or_8 (or_8_out, button_8_out, and_35_out);
  Hex_Digit_Display hex_digit_display_17 (.value(PA));  // open: dp
  _4bit_mem u_4bit_mem_3 (
    .CLK(or_8_out), .Enable(On), .Clear(RESET), .Preset(1'b0), .Q(PA), .D(adder_4_out));  // open: Preset_value
  _4bit_mem u_4bit_mem_4 (
    .CLK(and_36_out), .Enable(On), .Clear(RESET), .Preset(1'b0), .Q(PB), .D(adder_5_out));  // open: Preset_value
  and and_41 (and_41_out, nor_6_out, buffer_32_out);
  buf buffer_32 (buffer_32_out, buffer_33_out);
  buf buffer_33 (buffer_33_out, buffer_34_out);
  buf buffer_34 (buffer_34_out, buffer_35_out);
  nor nor_6 (nor_6_out, UMB[0], UMB[1], UMB[2], UMB[3]);
  buf buffer_35 (buffer_35_out, buffer_36_out);
  buf buffer_36 (buffer_36_out, nand_6_out);
  nand nand_6 (nand_6_out, UMB[0], UMB[1], UMB[2], UMB[3]);
  cont_0_9 cont_0_9_3 (
    .CLK(cont_0_5_4_c_out), .Enable(B_jogando), .Clear(clr), .Preset_value(in_2), .Q(UMB),
    .C_out(cont_0_9_3_c_out), .Preset(prst));
  and and_42 (and_42_out, ~B_Out, ~A_Out, toggle_3_out_3);  // AND_Gate
  or or_9 (or_9_out, and_42_out, and_43_out);
  and and_43 (and_43_out, A_Out, ~B_Out);  // AND_Gate
  or or_10 (clr, and_39_out, RESET);
  Multiplexer #(.width(4), .disabled(0), .enable("false")) multiplexer_5 (
    .in0(DA), .in1(DB), .out(multiplexer_5_out), .sel(Jogador));
  Adder #(.width(4)) adder_4 (.a(PA), .b(4'b0001), .out(adder_4_out));  // open: cin, cout
  Adder #(.width(4)) adder_5 (.a(PB), .b(4'b0001), .out(adder_5_out));  // open: cin, cout
  and and_44 (B_Out, and_37_out, and_41_out, and_45_out, and_46_out);
  cont_0_5 cont_0_5_4 (
    .CLK(cont_0_9_4_c_out), .Enable(B_jogando), .Clear(clr), .Preset_value(in_3), .Q(DSB),
    .C_out(cont_0_5_4_c_out), .Preset(prst));
  buf buffer_37 (Jogador, or_9_out);
  and and_45 (and_45_out, nor_7_out, buffer_38_out);
  buf buffer_38 (buffer_38_out, buffer_39_out);
  buf buffer_39 (buffer_39_out, buffer_40_out);
  buf buffer_40 (buffer_40_out, buffer_41_out);
  nor nor_7 (nor_7_out, DSB[0], DSB[1], DSB[2], DSB[3]);
  buf buffer_41 (buffer_41_out, buffer_42_out);
  buf buffer_42 (buffer_42_out, nand_7_out);
  nand nand_7 (nand_7_out, DSB[0], DSB[1], DSB[2], DSB[3]);
  cont_0_9 cont_0_9_4 (
    .CLK(CLK), .Enable(B_jogando), .Clear(clr), .Preset_value(in_4), .Q(USB), .C_out(cont_0_9_4_c_out),
    .Preset(prst));
  nor nor_8 (nor_8_out, USB[0], USB[1], USB[2], USB[3]);
  nand nand_8 (nand_8_out, USB[0], USB[1], USB[2], USB[3]);
  and and_46 (and_46_out, nor_8_out, buffer_43_out);
  buf buffer_43 (buffer_43_out, buffer_44_out);
  buf buffer_44 (buffer_44_out, buffer_45_out);
  buf buffer_45 (buffer_45_out, buffer_46_out);
  buf buffer_46 (buffer_46_out, buffer_47_out);
  buf buffer_47 (buffer_47_out, nand_8_out);

  // Other names for the same wires on the sheet: a0 = in_12; a1 = in_11; a2 = in_10; b0 = in_8; b1 = in_7; b2 = in_6;
  //   a3 = in_9; SA = in_9; b3 = in_5; SB = in_5; dm[3:0] = in_1; ds[3:0] = in_3; enA = A_jogando; enB = B_jogando;
  //   um[3:0] = in_2; us[3:0] = in_4; Xr[3] = SX; Yr[3] = SY

  // Notes on the sheet:
  //   Display de A e B
  //   Gerador das Coordenadas
  //   Ativador do Clock
  //   Aternador de Jogador
  //   Relógio de A
  //   Circuito do Fim do Jogo
  //   Configuração do Relógio
  //   Detector de Acerto
  //   Display dos Pontos
  //   Comparador da  Soma
  //   Display do Chute
  //   Relógio de B
  //   Mudador de fases
endmodule

module latch (
  input  D,
  input  CLK,
  input  Enable,
  input  Clear,
  input  Preset,
  output Q
);

  wire and_1_out, buffer_1_out, buffer_2_out, nor_2_out, R_out, S_out;

  buf buffer_1 (buffer_1_out, CLK);
  buf buffer_2 (buffer_2_out, buffer_1_out);
  and and_1 (and_1_out, CLK, ~buffer_2_out, Enable);  // AND_Gate
  and R (R_out, ~D, and_1_out);  // AND_Gate
  and S (S_out, and_1_out, D);
  nor nor_1 (Q, R_out, Clear, nor_2_out);
  nor nor_2 (nor_2_out, Q, S_out, Preset);
endmodule

module _4bit_mem (
  input  CLK,
  input  Enable,
  input  Clear,
  input  [3:0] D,
  input  Preset,
  input  [3:0] Preset_value,
  output [3:0] Q
);

  wire [3:0] multiplexer_1_out;

  Multiplexer #(.width(4), .disabled(0)) multiplexer_1 (
    .in1(Preset_value), .out(multiplexer_1_out), .sel(Preset), .en(Preset));  // open: in0
  D_Flip_Flop d_ff_1 (
    .clk(CLK), .D(D[3]), .Q(Q[3]), .preset(multiplexer_1_out[3]), .en(Enable), .reset(Clear));  // open: Qn
  D_Flip_Flop d_ff_2 (
    .clk(CLK), .D(D[2]), .Q(Q[2]), .preset(multiplexer_1_out[2]), .en(Enable), .reset(Clear));  // open: Qn
  D_Flip_Flop d_ff_3 (
    .clk(CLK), .D(D[0]), .Q(Q[0]), .preset(multiplexer_1_out[0]), .en(Enable), .reset(Clear));  // open: Qn
  D_Flip_Flop d_ff_4 (
    .clk(CLK), .D(D[1]), .Q(Q[1]), .preset(multiplexer_1_out[1]), .en(Enable), .reset(Clear));  // open: Qn
endmodule

module cont_0_9 (
  input  CLK,
  input  Enable,
  input  Clear,
  input  [3:0] Preset_value,
  input  Preset,
  output [3:0] Q,
  output C_out
);

  wire and_2_out, buffer_1_out, buffer_2_out, buffer_3_out, or_1_out, or_2_out, or_3_out;
  wire [3:0] adder_1_out, multiplexer_1_out;

  buf buffer_1 (buffer_1_out, C_out);
  buf buffer_2 (buffer_2_out, buffer_1_out);
  and and_1 (C_out, Q[0], Q[1], Q[2], Q[3]);
  or or_1 (or_1_out, and_2_out, Preset);
  and and_2 (and_2_out, C_out, ~buffer_2_out);  // AND_Gate
  _4bit_mem u_4bit_mem_1 (
    .CLK(CLK), .Enable(Enable), .Clear(or_2_out), .Preset(buffer_3_out), .Q(Q),
    .Preset_value(multiplexer_1_out), .D(adder_1_out));
  or or_2 (or_2_out, Clear, or_1_out);
  buf buffer_3 (buffer_3_out, or_3_out);
  or or_3 (or_3_out, and_2_out, Preset);
  Multiplexer #(.width(4), .disabled(0), .enable("false")) multiplexer_1 (
    .in0(4'b1001), .in1(Preset_value), .out(multiplexer_1_out), .sel(Preset));
  Adder #(.width(4)) adder_1 (.a(Q), .b(4'b1111), .out(adder_1_out));  // open: cin, cout
endmodule

module cont_0_5 (
  input  CLK,
  input  Enable,
  input  Clear,
  input  [3:0] Preset_value,
  input  Preset,
  output [3:0] Q,
  output C_out
);

  wire and_2_out, buffer_1_out, buffer_2_out, buffer_3_out, or_1_out, or_2_out, or_3_out;
  wire [3:0] adder_1_out, multiplexer_1_out;

  buf buffer_1 (buffer_1_out, buffer_2_out);
  buf buffer_2 (buffer_2_out, C_out);
  and and_1 (C_out, Q[0], Q[1], Q[2], Q[3]);
  or or_1 (or_1_out, and_2_out, Preset);
  and and_2 (and_2_out, C_out, ~buffer_1_out);  // AND_Gate
  _4bit_mem u_4bit_mem_1 (
    .CLK(CLK), .Enable(Enable), .Clear(or_2_out), .Preset(buffer_3_out), .Q(Q),
    .Preset_value(multiplexer_1_out), .D(adder_1_out));
  or or_2 (or_2_out, Clear, or_1_out);
  buf buffer_3 (buffer_3_out, or_3_out);
  Multiplexer #(.width(4), .disabled(0), .enable("false")) multiplexer_1 (
    .in0(4'b0101), .in1(Preset_value), .out(multiplexer_1_out), .sel(Preset));
  or or_3 (or_3_out, and_2_out, Preset);
  Adder #(.width(4)) adder_1 (.a(Q), .b(4'b1111), .out(adder_1_out));  // open: cin, cout
endmodule

module toggle (
  input  in_1,
  input  in_2,
  output out_3
);

  wire and_1_out, and_2_out, buffer_1_out, buffer_2_out, buffer_3_out, nor_2_out, not_1_out, not_2_out,
       not_3_out, R_out, S_out;

  not not_1 (not_1_out, buffer_1_out);
  buf buffer_1 (buffer_1_out, in_1);
  not not_2 (not_2_out, out_3);
  and and_1 (and_1_out, in_1, not_1_out);
  buf buffer_2 (buffer_2_out, in_2);
  and R (R_out, ~not_2_out, and_1_out);  // AND_Gate
  buf buffer_3 (buffer_3_out, and_2_out);
  and S (S_out, and_1_out, not_2_out);
  and and_2 (and_2_out, in_2, not_3_out);
  not not_3 (not_3_out, buffer_2_out);
  nor nor_1 (out_3, R_out, buffer_3_out, nor_2_out);
  nor nor_2 (nor_2_out, out_3, and_2_out, S_out);
endmodule
