// Logisim project Projeto de Circuitos.circ as structural Verilog: 5 circuits, main circuit main
module main (
  input  in_1,
  input  in_2,
  input  in_3,
  input  in_4,
  input  in_5,
  input  in_6,
  input  in_7,
  input  in_8,
  input  Jogador,
  output x,
  output x_2,
  output x_3
);

  wire button_1_out, displaydecoder_1_a, displaydecoder_1_b, displaydecoder_1_c, displaydecoder_1_d,
       displaydecoder_1_e, displaydecoder_1_f, displaydecoder_1_g, displaydecoder_2_a, displaydecoder_2_b,
       displaydecoder_2_c, displaydecoder_2_d, displaydecoder_2_e, displaydecoder_2_f, displaydecoder_2_g,
       Jogar_out, multiplexador_1_out_10, multiplexador_1_out_11, multiplexador_1_out_12,
       multiplexador_1_out_13;
  wire [3:0] rng_1_out_2;

  _7_Segment_Display u_7_segment_display_1 (
    .g(displaydecoder_1_g), .f(displaydecoder_1_f), .a(displaydecoder_1_a), .b(displaydecoder_1_b),
    .e(displaydecoder_1_e), .d(displaydecoder_1_d), .c(displaydecoder_1_c));  // open: dp
  _7_Segment_Display u_7_segment_display_2 (
    .g(displaydecoder_2_g), .f(displaydecoder_2_f), .a(displaydecoder_2_a), .b(displaydecoder_2_b),
    .e(displaydecoder_2_e), .d(displaydecoder_2_d), .c(displaydecoder_2_c));  // open: dp
  DisplayDecoder displaydecoder_1 (
    .A(displaydecoder_1_a), .B(displaydecoder_1_b), .C(displaydecoder_1_c), .D(displaydecoder_1_d),
    .E(displaydecoder_1_e), .F(displaydecoder_1_f), .G(displaydecoder_1_g), .in_1(in_1), .in_2(in_2),
    .in_3(in_3), .in_4(in_4));
  DisplayDecoder displaydecoder_2 (
    .A(displaydecoder_2_a), .B(displaydecoder_2_b), .C(displaydecoder_2_c), .D(displaydecoder_2_d),
    .E(displaydecoder_2_e), .F(displaydecoder_2_f), .G(displaydecoder_2_g), .in_1(in_5), .in_2(in_6),
    .in_3(in_7), .in_4(in_8));
  Multiplexador multiplexador_1 (
    .A(in_1), .B(in_2), .C(in_3), .D(in_4), .A_2(in_5), .B_2(in_6), .C_2(in_7), .D_2(in_8),
    .out_10(multiplexador_1_out_10), .out_11(multiplexador_1_out_11), .out_12(multiplexador_1_out_12),
    .out_13(multiplexador_1_out_13), .in_9(Jogador));
  Button Jogar (.out(Jogar_out));
  RNG rng_1 (.in_1(button_1_out), .out_2(rng_1_out_2));
  Button button_1 (.out(button_1_out));
  Comparador comparador_1 (
    .in_1(multiplexador_1_out_10), .in_2(multiplexador_1_out_11), .in_3(multiplexador_1_out_12),
    .in_4(multiplexador_1_out_13), .in_6(Jogar_out), .out_7(x), .out_8(x_2), .out_9(x_3), .in_5(rng_1_out_2));
endmodule

module Multiplexador (
  input  A,
  input  B,
  input  C,
  input  D,
  input  A_2,
  input  B_2,
  input  C_2,
  input  D_2,
  input  in_9,
  output out_10,
  output out_11,
  output out_12,
  output out_13
);

  wire and_1_out, and_2_out, and_3_out, and_4_out, and_5_out, and_6_out, and_7_out, and_8_out;

  and and_1 (and_1_out, A, ~in_9);  // AND_Gate
  and and_2 (and_2_out, B, ~in_9);  // AND_Gate
  and and_3 (and_3_out, C, ~in_9);  // AND_Gate
  and and_4 (and_4_out, D, ~in_9);  // AND_Gate
  and and_5 (and_5_out, A_2, in_9);
  and and_6 (and_6_out, B_2, in_9);
  and and_7 (and_7_out, C_2, in_9);
  and and_8 (and_8_out, D_2, in_9);
  or or_1 (out_10, and_1_out, and_5_out);
  or or_2 (out_11, and_2_out, and_6_out);
  or or_3 (out_12, and_3_out, and_7_out);
  or or_4 (out_13, and_4_out, and_8_out);
endmodule

module DisplayDecoder (
  input  in_1,
  input  in_2,
  input  in_3,
  input  in_4,
  output A,
  output B,
  output C,
  output D,
  output E,
  output F,
  output G
);

  wire and_1_out, and_2_out, and_3_out, and_4_out, and_5_out, and_6_out, and_7_out, and_8_out, and_9_out,
       and_10_out, and_11_out, and_12_out, and_13_out, and_14_out, and_15_out, and_16_out, and_17_out,
       and_18_out, and_19_out, and_20_out, and_21_out, and_22_out, and_23_out, and_24_out, and_25_out,
       and_26_out, and_27_out, and_28_out, and_29_out, and_30_out, and_31_out, and_32_out, and_33_out,
       and_34_out, and_35_out, and_36_out, and_37_out;

  and and_1 (and_1_out, in_3, ~in_4);  // AND_Gate
  and and_2 (and_2_out, in_2, in_3);
  and and_3 (and_3_out, in_1, ~in_4);  // AND_Gate
  and and_4 (and_4_out, ~in_2, ~in_4);  // AND_Gate
  and and_5 (and_5_out, ~in_1, in_3);  // AND_Gate
  and and_6 (and_6_out, ~in_1, in_2, in_4);  // AND_Gate
  and and_7 (and_7_out, in_1, ~in_2, ~in_3);  // AND_Gate
  and and_8 (and_8_out, ~in_1, ~in_2);  // AND_Gate
  and and_9 (and_9_out, ~in_2, ~in_3);  // AND_Gate
  and and_10 (and_10_out, ~in_2, ~in_4);  // AND_Gate
  and and_11 (and_11_out, in_1, ~in_3, in_4);  // AND_Gate
  and and_12 (and_12_out, ~in_1, in_3, in_4);  // AND_Gate
  and and_13 (and_13_out, ~in_1, ~in_3, ~in_4);  // AND_Gate
  and and_14 (and_14_out, in_1, ~in_2);  // AND_Gate
  and and_15 (and_15_out, ~in_1, in_2);  // AND_Gate
  and and_16 (and_16_out, ~in_3, in_4);  // AND_Gate
  and and_17 (and_17_out, ~in_1, ~in_3);  // AND_Gate
  and and_18 (and_18_out, ~in_1, in_4);  // AND_Gate
  and and_19 (and_19_out, in_1, ~in_3);  // AND_Gate
  and and_20 (and_20_out, ~in_1, ~in_2, ~in_4);  // AND_Gate
  and and_21 (and_21_out, in_2, ~in_3, in_4);  // AND_Gate
  and and_22 (and_22_out, ~in_2, in_3, in_4);  // AND_Gate
  and and_23 (and_23_out, in_2, in_3, ~in_4);  // AND_Gate
  and and_24 (and_24_out, in_3, ~in_4);  // AND_Gate
  and and_25 (and_25_out, in_1, in_2);
  and and_26 (and_26_out, ~in_2, ~in_4);  // AND_Gate
  and and_27 (and_27_out, in_1, in_3);
  and and_28 (and_28_out, ~in_3, ~in_4);  // AND_Gate
  and and_29 (and_29_out, in_1, ~in_2);  // AND_Gate
  and and_30 (and_30_out, in_1, in_3);
  and and_31 (and_31_out, in_2, in_3, ~in_4);  // AND_Gate
  and and_32 (and_32_out, ~in_1, in_2, ~in_3);  // AND_Gate
  and and_33 (and_33_out, in_3, ~in_4);  // AND_Gate
  and and_34 (and_34_out, in_1, ~in_2);  // AND_Gate
  and and_35 (and_35_out, in_1, in_4);
  and and_36 (and_36_out, ~in_2, in_3);  // AND_Gate
  and and_37 (and_37_out, ~in_1, in_2, ~in_3);  // AND_Gate
  or or_1 (A, and_1_out, and_2_out, and_3_out, and_4_out, and_5_out, and_6_out, and_7_out);
  or or_2 (B, and_8_out, and_9_out, and_10_out, and_11_out, and_12_out, and_13_out);
  or or_3 (C, and_14_out, and_15_out, and_16_out, and_17_out, and_18_out);
  or or_4 (D, and_19_out, and_20_out, and_21_out, and_22_out, and_23_out);
  or or_5 (E, and_24_out, and_25_out, and_26_out, and_27_out);
  or or_6 (F, and_28_out, and_29_out, and_30_out, and_31_out, and_32_out);
  or or_7 (G, and_33_out, and_34_out, and_35_out, and_36_out, and_37_out);
endmodule

module Comparador (
  input  in_1,
  input  in_2,
  input  in_3,
  input  in_4,
  input  [3:0] in_5,
  input  in_6,
  output out_7,
  output out_8,
  output out_9
);

  wire and_1_out, and_2_out, and_3_out, and_4_out, or_1_out, xnor_1_out, xnor_2_out, xnor_3_out, xnor_4_out;

  xnor xnor_1 (xnor_1_out, in_1, in_5[0]);
  xnor xnor_2 (xnor_2_out, in_2, in_5[1]);
  xnor xnor_3 (xnor_3_out, in_3, in_5[2]);
  xnor xnor_4 (xnor_4_out, in_4, in_5[3]);
  and and_1 (and_1_out, in_1, ~in_5[0]);  // AND_Gate
  and and_2 (and_2_out, in_2, xnor_1_out, ~in_5[1]);  // AND_Gate
  and and_3 (and_3_out, in_3, ~in_5[2], xnor_1_out, xnor_2_out);  // AND_Gate
  and and_4 (and_4_out, in_4, ~in_5[3], xnor_1_out, xnor_2_out, xnor_3_out);  // AND_Gate
  or or_1 (or_1_out, and_1_out, and_2_out, and_3_out, and_4_out);
  and and_5 (out_7, or_1_out, in_6);
  and and_6 (out_8, xnor_1_out, xnor_2_out, in_6, xnor_3_out, xnor_4_out);
  and and_7 (out_9, ~out_8, ~out_7, in_6);  // AND_Gate
endmodule

module RNG (
  input  in_1,
  output [3:0] out_2
);

  Random #(.width(4), .trigger("falling")) random_1 (.clk(in_1), .out(out_2));  // open: next, clr
endmodule
